// Logisim project adh0.circ as structural Verilog
module ALU (
  input  CLK,
  input  CS_FRI,
  input  CS_ALUOP1,
  input  CS_ALUOP0,
  input  nRST,
  input  [7:0] A,
  input  [7:0] B,
  output F_C,
  output F_B,
  output [7:0] C
);

  wire adders_pin1, adders_pin4, adders_pin10, adders_pin13, inv_pin3, inv_pin6, inv_pin8, inv_pin11,
       n7400_1_pin4, n7400_1_pin6, n7400_1_pin8, n7408_1_pin3, n7408_1_pin5, n7408_1_pin6, n7408_1_pin8,
       n7408_1_pin11, n7432_1_pin11, n7442_1_pin1, n7442_1_pin2, n7442_1_pin12, n7442_1_pin13, n7486_1_pin2,
       n7486_1_pin3, n7486_1_pin6, n7486_1_pin8, n7486_1_pin11, n74175_1_pin4, n74175_1_pin5, n74283_1_pin1,
       n74283_1_pin4, n74283_1_pin7, n74283_1_pin10, n74283_1_pin13;

  _7442 #(.ShowInternalStructure("true")) u_7442_1 (
    .pin1(n7442_1_pin1), .pin2(n7442_1_pin2), .pin15(CS_ALUOP0), .pin14(CS_ALUOP1), .pin13(n7442_1_pin13),
    .pin12(n7442_1_pin12));  // open: pin3, pin4, pin5, pin6, pin7, pin11, pin10, pin9
  _7486 #(.ShowInternalStructure("true")) u_7486_1 (
    .pin1(B[4]), .pin2(n7486_1_pin2), .pin3(n7486_1_pin3), .pin4(B[5]), .pin5(n7486_1_pin2),
    .pin6(n7486_1_pin6), .pin13(B[7]), .pin12(n7486_1_pin2), .pin11(n7486_1_pin11), .pin10(B[6]),
    .pin9(n7486_1_pin2), .pin8(n7486_1_pin8));
  _7400 #(.ShowInternalStructure("true")) u_7400_1 (
    .pin1(n7442_1_pin2), .pin2(n7442_1_pin2), .pin3(n7486_1_pin2), .pin4(n7400_1_pin4), .pin5(n7400_1_pin4),
    .pin6(n7400_1_pin6), .pin10(n7442_1_pin1), .pin9(n7442_1_pin1), .pin8(n7400_1_pin8));  // open: pin13, pin12, pin11
  _7486 #(.ShowInternalStructure("true")) inv (
    .pin1(B[0]), .pin2(n7486_1_pin2), .pin3(inv_pin3), .pin4(B[1]), .pin5(n7486_1_pin2), .pin6(inv_pin6),
    .pin13(B[3]), .pin12(n7486_1_pin2), .pin11(inv_pin11), .pin10(B[2]), .pin9(n7486_1_pin2), .pin8(inv_pin8));
  _7408 #(.ShowInternalStructure("true")) u_7408_1 (
    .pin1(n7442_1_pin2), .pin2(n7442_1_pin1), .pin3(n7408_1_pin3), .pin4(n7486_1_pin2), .pin5(n7408_1_pin5),
    .pin6(n7408_1_pin6), .pin13(CS_FRI), .pin12(CLK), .pin11(n7408_1_pin11), .pin10(n7400_1_pin8),
    .pin9(F_C), .pin8(n7408_1_pin8));
  _74175 #(.ShowInternalStructure("true")) u_74175_1 (
    .pin1(nRST), .pin2(n7408_1_pin5), .pin3(F_B), .pin4(n74175_1_pin4), .pin5(n74175_1_pin5), .pin6(F_C),
    .pin9(n7408_1_pin11));  // open: pin7, pin15, pin14, pin13, pin12, pin11, pin10
  _74283 #(.ShowInternalStructure("true")) u_74283_1 (
    .pin1(n74283_1_pin1), .pin2(n7486_1_pin6), .pin3(A[4]), .pin4(n74283_1_pin4), .pin5(A[3]),
    .pin6(n7486_1_pin3), .pin7(n74283_1_pin7), .pin15(n7486_1_pin8), .pin14(A[6]), .pin13(n74283_1_pin13),
    .pin12(A[7]), .pin11(n7486_1_pin11), .pin10(n74283_1_pin10), .pin9(n7400_1_pin4));
  _7432 #(.ShowInternalStructure("true")) u_7432_1 (
    .pin1(n7442_1_pin1), .pin2(n7400_1_pin6), .pin3(n74175_1_pin5), .pin4(n7400_1_pin4), .pin5(n7442_1_pin2),
    .pin6(n74175_1_pin4), .pin13(n7408_1_pin8), .pin12(n7408_1_pin6), .pin11(n7432_1_pin11));  // open: pin10, pin9, pin8
  _74283 #(.ShowInternalStructure("true")) adders (
    .pin1(adders_pin1), .pin2(inv_pin6), .pin3(A[1]), .pin4(adders_pin4), .pin5(A[0]), .pin6(inv_pin3),
    .pin7(n7432_1_pin11), .pin15(inv_pin8), .pin14(A[2]), .pin13(adders_pin13), .pin12(A[3]),
    .pin11(inv_pin11), .pin10(adders_pin10), .pin9(n74283_1_pin7));
  _74244 #(.ShowInternalStructure("true")) u_74244_1 (
    .pin1(n7408_1_pin3), .pin2(n74283_1_pin1), .pin3(C[6]), .pin4(n74283_1_pin4), .pin5(C[7]),
    .pin6(adders_pin1), .pin7(C[2]), .pin8(adders_pin4), .pin9(C[3]), .pin19(n7408_1_pin3), .pin18(C[5]),
    .pin17(n74283_1_pin13), .pin16(C[4]), .pin15(n74283_1_pin10), .pin14(C[1]), .pin13(adders_pin13),
    .pin12(C[0]), .pin11(adders_pin10));
  // also tied to GND on the sheet: {n7442_1_pin13, n7442_1_pin12}
endmodule

module AT28C64B (
  input  A0,
  input  A1,
  input  A2,
  input  A3,
  input  A4,
  input  A5,
  input  A6,
  input  A7,
  input  A8,
  input  A9,
  input  A10,
  input  A11,
  input  A12,
  input  CE_N,
  input  WE_N,
  input  OE_N,
  input  I0,
  input  I1,
  input  I2,
  input  I3,
  input  I4,
  input  I5,
  input  I6,
  input  I7,
  output O0,
  output O1,
  output O2,
  output O3,
  output O4,
  output O5,
  output O6,
  output O7
);

  wire nor_1_out, nor_2_out, not_1_out;
  wire [7:0] ram_1_dout;
  wire [12:0] controlled_buffer_1_out;

  nor nor_1 (nor_1_out, CE_N, WE_N);
  not not_1 (not_1_out, CE_N);
  nor nor_2 (nor_2_out, CE_N, OE_N);
  assign controlled_buffer_1_out = not_1_out ? {A12, A11, A10, A9, A8, A7, A6, A5, A4, A3, A2, A1, A0} : 13'bz;  // Controlled_Buffer controlled_buffer_1
  RAM #(.addrWidth(13), .trigger("high")) ram_1 (
    .addr(controlled_buffer_1_out), .we(nor_1_out), .oe(nor_2_out), .din({I7, I6, I5, I4, I3, I2, I1, I0}),
    .dout(ram_1_dout));
  assign {O7, O6, O5, O4, O3, O2, O1, O0} = nor_2_out ? ram_1_dout : 8'bz;  // Controlled_Buffer controlled_buffer_2
endmodule
